# Fritzing sketch eeprom prgramming (saved by Fritzing 0.9.3b)
breadboards: 1

parts:
  Part1 = Arduino Nano (Rev3.0)
  IC1 = IC, DIP package, 8 pins [chip_label=IC]
  R1 = Resistor [tolerance=±5% resistance=4.7k package=THT]
  R2 = Resistor [tolerance=±5% resistance=4.7k package=THT]

nets:
  N1: Part1.GND, IC1.pin1, IC1.pin2, IC1.pin3, IC1.pin4, IC1.pin7
  N2: Part1.A5, IC1.pin6, R1.Pin_1
  N3: Part1.A4, IC1.pin5, R2.Pin_1
  N4: Part1.3V3, IC1.pin8, R1.Pin_0, R2.Pin_0
